// Logisim project Saguii.circ as structural Verilog: 5 circuits, main circuit main
module main (
);

  wire button_1_out, button_2_out, CI, CLK, r0, RS, ula_1_comp, WM, WR;
  wire [1:0] multiplexer_2_out, PcSource, separa_1_ra, separa_1_rb;
  wire [3:0] separa_1_opcode, ula_ctrl;
  wire [7:0] adder_1_out, adder_2_out, bd_1_da, db, imm, multiplexer_1_out, multiplexer_3_out,
       multiplexer_4_out, ram_1_dout, register_1_q, rom_1_data, ula_out;

  Clock clock_1 (.out(CLK));
  Register register_1 (.D(multiplexer_1_out), .en(1'b1), .clk(CLK), .Q(register_1_q), .clr(button_1_out));
  Button button_1 (.out(button_1_out));
  ROM rom_1 (.addr(register_1_q), .data(rom_1_data));
  Adder adder_1 (.a(imm), .b(register_1_q), .out(adder_1_out));  // open: cin, cout
  Adder adder_2 (.a(8'h1), .b(register_1_q), .out(adder_2_out));  // open: cin, cout
  Multiplexer #(.select(2), .width(8)) multiplexer_1 (
    .in0(adder_1_out), .in1(adder_2_out), .in2(db), .in3(db), .out(multiplexer_1_out), .sel(PcSource));
  separa separa_1 (.instr(rom_1_data), .opcode(separa_1_opcode), .ra(separa_1_ra), .rb(separa_1_rb), .imm(imm));
  Multiplexer #(.width(2)) multiplexer_2 (.in0(separa_1_ra), .in1(2'b00), .out(multiplexer_2_out), .sel(r0));
  // Probe on separa_1_rb
  // Probe on multiplexer_4_out
  // Probe on multiplexer_2_out
  Button button_2 (.out(button_2_out));
  UC uc_1 (
    .OPCODE(separa_1_opcode), .comp(ula_1_comp), .WM(WM), .pc_source(PcSource), .RS(RS), .r0(r0), .CI(CI),
    .WR(WR), .ula_ctrl(ula_ctrl));
  BD bd_1 (
    .CLK(CLK), .WD(multiplexer_4_out), .ra(multiplexer_2_out), .WR(WR), .WA(multiplexer_2_out),
    .rb(separa_1_rb), .R(button_2_out), .da(bd_1_da), .db(db));
  Multiplexer #(.width(8)) multiplexer_3 (.in0(db), .in1(imm), .out(multiplexer_3_out), .sel(CI));
  // Probe on bd_1_da
  ULA ula_1 (.ula_ctrl(ula_ctrl), .op1(bd_1_da), .op2(multiplexer_3_out), .comp(ula_1_comp), .ula_out(ula_out));
  // Probe on db
  RAM #(.enables("line")) ram_1 (.addr(db), .we(WM), .clk(CLK), .din(bd_1_da), .dout(ram_1_dout));
  Multiplexer #(.width(8)) multiplexer_4 (.in0(ula_out), .in1(ram_1_dout), .out(multiplexer_4_out), .sel(RS));
  // Probe on RS
  // Probe on ram_1_dout

  // Notes on the sheet:
  //   contents of rom_1 (hex, n*v repeats v):
  //   70 80 64 81 6c 68 8a 16 5d 9c a2 96 3b 8a 6c fe 16 5d 9e a2 96 3b 64 8a 68 8d 72 c 4d 42 9c 8a 70 98
  //   5e 89 a8 81 94 8a 6c ad 89 71 20 30
endmodule

module separa (
  input  [7:0] instr,
  output [3:0] opcode,
  output [1:0] ra,
  output [1:0] rb,
  output [7:0] imm
);

  assign imm = {{4{instr[3]}}, instr[3:0]};  // Bit_Extender bit_extender_1

  assign opcode = instr[7:4];
  assign ra = instr[3:2];
  assign rb = instr[1:0];

  // Notes on the sheet:
  //   rb
endmodule

module BD (
  input  CLK,
  input  [7:0] WD,
  input  [1:0] ra,
  input  WR,
  input  [1:0] WA,
  input  [1:0] rb,
  input  R,
  output [7:0] da,
  output [7:0] db
);

  wire demultiplexer_1_out0, demultiplexer_1_out1, demultiplexer_1_out2, demultiplexer_1_out3;
  wire [7:0] register_1_q, register_2_q, register_3_q, register_4_q;

  Demultiplexer #(.select(2)) demultiplexer_1 (
    .out0(demultiplexer_1_out0), .out1(demultiplexer_1_out1), .out2(demultiplexer_1_out2),
    .out3(demultiplexer_1_out3), .in(WR), .sel(WA));
  Register register_1 (.D(WD), .en(demultiplexer_1_out0), .clk(CLK), .Q(register_1_q), .clr(R));
  Register register_2 (.D(WD), .en(demultiplexer_1_out1), .clk(CLK), .Q(register_2_q), .clr(R));
  Register register_3 (.D(WD), .en(demultiplexer_1_out2), .clk(CLK), .Q(register_3_q), .clr(R));
  Register register_4 (.D(WD), .en(demultiplexer_1_out3), .clk(CLK), .Q(register_4_q), .clr(R));
  Multiplexer #(.select(2), .width(8)) multiplexer_1 (
    .in0(register_1_q), .in1(register_2_q), .in2(register_3_q), .in3(register_4_q), .out(da), .sel(ra));
  Multiplexer #(.select(2), .width(8)) multiplexer_2 (
    .in0(register_1_q), .in1(register_2_q), .in2(register_3_q), .in3(register_4_q), .out(db), .sel(rb));
endmodule

module ULA (
  input  [3:0] ula_ctrl,
  input  [7:0] op1,
  input  [7:0] op2,
  output comp,
  output [7:0] ula_out
);

  wire [7:0] adder_1_out, and_1_out, bit_extender_1_out, not_1_out, or_1_out, shifter_1_out, shifter_2_out,
       subtractor_1_out;

  Comparator comparator_1 (.a(op1), .b({8{1'b0}}), .eq(comp));  // open: gt, lt
  Adder adder_1 (.a(op1), .b(op2), .out(adder_1_out));  // open: cin, cout
  Subtractor subtractor_1 (.a(op1), .b(op2), .out(subtractor_1_out));  // open: bin, bout
  assign and_1_out = op1 & op2;  // AND_Gate and_1, 8 bits wide
  assign or_1_out = op1 | op2;  // OR_Gate or_1, 8 bits wide
  assign not_1_out = ~op2;  // NOT_Gate not_1, 8 bits wide
  Shifter shifter_1 (.in(op1), .\dist (op2[2:0]), .out(shifter_1_out));
  Shifter #(.shift("ar")) shifter_2 (.in(op1), .\dist (op2[2:0]), .out(shifter_2_out));
  assign bit_extender_1_out = {{7{comp}}, comp};  // Bit_Extender bit_extender_1
  Multiplexer #(.select(4), .width(8)) multiplexer_1 (
    .in0(bit_extender_1_out), .in6(op2), .in7({op2[3:0], op1[3:0]}), .in8({op1[7:4], op2[3:0]}),
    .in9(adder_1_out), .in10(subtractor_1_out), .in11(and_1_out), .in12(or_1_out), .in13(not_1_out),
    .in14(shifter_1_out), .in15(shifter_2_out), .out(ula_out), .sel(ula_ctrl));  // open: in1, in2, in3, in4, in5

  // Notes on the sheet:
  //   mov
  //   movh
  //   movL
endmodule

module UC (
  input  [3:0] OPCODE,
  input  comp,
  output WM,
  output [1:0] pc_source,
  output RS,
  output r0,
  output CI,
  output WR,
  output [3:0] ula_ctrl
);

  wire and_2_out, and_3_out, and_9_out, and_10_out, and_11_out, and_12_out, and_13_out, and_14_out,
       and_15_out, and_16_out, and_17_out, and_18_out, bi, br, ji, jr, not_1_out, not_2_out, not_3_out,
       not_4_out, not_5_out, not_6_out, not_7_out, not_8_out, not_9_out, not_10_out, not_11_out, not_12_out,
       not_13_out, not_14_out, not_15_out, not_16_out, not_17_out, not_18_out, not_19_out, not_20_out,
       not_21_out, not_22_out, not_23_out, not_24_out, not_25_out, not_26_out, not_27_out, not_28_out,
       not_29_out, not_30_out, not_31_out, not_32_out, not_33_out, not_34_out, not_35_out;

  not not_1 (not_1_out, OPCODE[0]);
  not not_2 (not_2_out, OPCODE[2]);
  not not_3 (not_3_out, OPCODE[3]);
  not not_4 (not_4_out, OPCODE[0]);
  not not_5 (not_5_out, OPCODE[0]);
  not not_6 (not_6_out, OPCODE[1]);
  not not_7 (not_7_out, OPCODE[2]);
  not not_8 (not_8_out, OPCODE[3]);
  not not_9 (not_9_out, OPCODE[1]);
  not not_10 (not_10_out, OPCODE[3]);
  not not_11 (not_11_out, OPCODE[1]);
  not not_12 (not_12_out, OPCODE[2]);
  not not_13 (not_13_out, OPCODE[3]);
  not not_14 (not_14_out, OPCODE[1]);
  not not_15 (not_15_out, OPCODE[2]);
  not not_16 (not_16_out, OPCODE[3]);
  not not_17 (not_17_out, OPCODE[2]);
  not not_18 (not_18_out, OPCODE[3]);
  not not_19 (not_19_out, OPCODE[1]);
  and and_1 (RS, not_5_out, not_19_out, not_20_out);
  not not_20 (not_20_out, OPCODE[3]);
  not not_21 (not_21_out, OPCODE[3]);
  not not_22 (not_22_out, OPCODE[0]);
  not not_23 (not_23_out, OPCODE[1]);
  not not_24 (not_24_out, OPCODE[2]);
  not not_25 (not_25_out, OPCODE[0]);
  not not_26 (not_26_out, OPCODE[1]);
  not not_27 (not_27_out, OPCODE[2]);
  not not_28 (not_28_out, OPCODE[3]);
  and and_2 (and_2_out, OPCODE[1], OPCODE[0]);
  and and_3 (and_3_out, OPCODE[0], OPCODE[3]);
  and and_4 (bi, OPCODE[0], not_11_out, not_12_out, not_13_out);
  and and_5 (br, not_1_out, not_14_out, not_15_out, not_16_out);
  and and_6 (ji, OPCODE[0], OPCODE[1], not_2_out, not_3_out);
  and and_7 (jr, not_4_out, OPCODE[1], not_17_out, not_18_out);
  or or_1 (ula_ctrl[0], and_2_out, and_3_out);
  and and_8 (WM, OPCODE[0], not_9_out, OPCODE[2], not_10_out);
  and and_9 (and_9_out, OPCODE[0], OPCODE[1], OPCODE[2], not_21_out);
  and and_10 (and_10_out, not_22_out, not_23_out, not_24_out, OPCODE[3]);
  and and_11 (and_11_out, OPCODE[0], not_6_out, not_7_out, not_8_out);
  and and_12 (and_12_out, not_25_out, not_26_out, not_27_out);
  and and_13 (and_13_out, not_28_out, OPCODE[0]);
  and and_14 (and_14_out, ~OPCODE[0], OPCODE[2]);  // AND_Gate
  and and_15 (and_15_out, OPCODE[2], OPCODE[1]);
  not not_29 (not_29_out, jr);
  not not_30 (not_30_out, ji);
  not not_31 (not_31_out, jr);
  not not_32 (not_32_out, ji);
  not not_33 (not_33_out, comp);
  not not_34 (not_34_out, br);
  not not_35 (not_35_out, bi);
  or or_2 (r0, and_9_out, and_10_out, and_11_out);
  or or_3 (CI, and_12_out, and_13_out);
  or or_4 (WR, and_14_out, OPCODE[3], and_15_out);
  and and_16 (and_16_out, br, comp);
  and and_17 (and_17_out, not_34_out, not_35_out, not_29_out, not_30_out);
  and and_18 (and_18_out, not_31_out, not_32_out, not_33_out);
  or or_5 (pc_source[1], and_16_out, jr);
  or or_6 (pc_source[0], and_17_out, and_18_out);

  assign ula_ctrl[3:1] = OPCODE[3:1];

  // Other names for the same wires on the sheet: op0 = OPCODE[0]; op1 = OPCODE[1]; op2 = OPCODE[2]; op3 = OPCODE[3]

  // Notes on the sheet:
  //   brzi
  //   brzr
  //   ji
  //   jr
endmodule
